// Digital circuit ALU.dig as structural Verilog
module ALU (
  input  [7:0] A,
  input  [7:0] B,
  input  SU,
  input  EO,
  output [7:0] out,
  output carry,
  output zero,
  output [7:0] EQL
);

  wire add_2_c_o, and_2_out, and_3_out, nor_1_out, nor_2_out, nor_3_out, nor_4_out;
  wire [3:0] add_1_s, add_2_s, xor_1_out;
  wire [7:4] xor_1_out_2;

  assign {xor_1_out_2, xor_1_out} = B ^ {8{SU}};  // XOr xor_1, 8 bits wide
  assign EQL = B & B;  // And and_1, 8 bits wide
  Add #(.Bits(4)) add_1 (.a(A[7:4]), .b(xor_1_out_2), .c_i(add_2_c_o), .s(add_1_s), .c_o(carry));
  Add #(.Bits(4)) add_2 (.a(A[3:0]), .b(xor_1_out), .c_i(SU), .s(add_2_s), .c_o(add_2_c_o));
  nor nor_1 (nor_1_out, add_2_s[0], add_2_s[1]);
  nor nor_2 (nor_2_out, add_2_s[2], add_2_s[3]);
  nor nor_3 (nor_3_out, add_1_s[0], add_1_s[1]);
  nor nor_4 (nor_4_out, add_1_s[2], add_1_s[3]);
  assign out = EO ? {add_1_s, add_2_s} : 8'bz;  // Driver driver_1
  and and_2 (and_2_out, nor_1_out, nor_2_out);
  and and_3 (and_3_out, nor_3_out, nor_4_out);
  and and_4 (zero, and_2_out, and_3_out);
endmodule
