// Digital circuit PC.dig as structural Verilog
module PC (
  input  CE,
  input  clk,
  input  [11:0] IN,
  input  J,
  output [10:0] OUT
);

  CounterPreset #(.Bits(11)) counterpreset_1 (
    .en(CE), .C(clk), .dir(1'b0), .in(IN[10:0]), .ld(J), .clr(1'b0), .out(OUT));  // open: ovf
endmodule
